# Fritzing sketch garage-lock (saved by Fritzing 1.0.4)

parts:
  ESP-12E = Gizwits WiFi Witty ESP-12F
  HLK-PM1 = HLK-PM01
  Input_24v_DC_Flashing_light = Camdenboss CTB0158-2 [part_number=CTB0158-2 package=THT]
  Output_220v_AC = Camdenboss CTB0158-2 [part_number=CTB0158-2 package=THT]
  Input_220v_AC = Camdenboss CTB0158-2 [part_number=CTB0158-2 package=THT]
  U1 = 2-Channel 5v Relay Shield [package=relay-2ch5v10a]
  R2 = Resistor [tolerance=±5% resistance=220 package="0603 [SMD]"]
  R3 = Resistor [tolerance=±5% resistance=220 package="2010 [SMD]"]
  12v_Gate_Electric_Lock = uhppote electric strike door lock
  AC/AC_220v_12v_Transformer = TRANSFORMER VB 1,5/1/9 [part_number="CROVISA 412935" package=transformer]
  Any_other_switch_appliance = Camdenboss CTB0158-2 [part_number=CTB0158-2 package=THT]

nets (from the breadboard view):
  N1: ESP-12E.GPIO14, R2.Pin_1, R3.Pin_1
  N2: ESP-12E.GPIO12, U1.IN1
  N3: ESP-12E.GPIO13, U1.IN2
  N4: ESP-12E.VCC, HLK-PM1.+Vo
  GND: ESP-12E.GND, HLK-PM1.-Vo, Input_24v_DC_Flashing_light.pin2, U1.GND, R3.Pin_0
  N5: HLK-PM1.AC#0, Input_220v_AC.pin2, U1.K2-In
  N6: HLK-PM1.AC#1, Output_220v_AC.pin2, Input_220v_AC.pin1, AC/AC_220v_12v_Transformer.3
  N7: Input_24v_DC_Flashing_light.pin1, R2.Pin_0
  N8: Output_220v_AC.pin1, U1.K2-On, AC/AC_220v_12v_Transformer.4
  N9: U1.K1-In, Any_other_switch_appliance.pin1
  N10: U1.K1-On, Any_other_switch_appliance.pin2
  N11: 12v_Gate_Electric_Lock.pin1, AC/AC_220v_12v_Transformer.1
  N12: 12v_Gate_Electric_Lock.pin2, AC/AC_220v_12v_Transformer.2

custom parts:
  2-Channel 5v Relay Shield: 2 Channel 5v Relay Shield w. 2x SPD-06VDC-SD-C
  uhppote electric strike door lock: UHPPOTE electric strike door lock.
  TRANSFORMER VB 1,5/1/9: 3,5VA/220vAC/12vAC Transformer
